// Logisim project lab4Solution.circ as structural Verilog: 2 circuits, main circuit main
module main (
  input  in_1,
  input  in_2,
  input  in_3,
  output out_4
);

  Multiplexer #(.select(2), .enable("false")) multiplexer_1 (
    .in0(1'b0), .in1(in_1), .in2(in_1), .in3(1'b1), .out(out_4), .sel({in_3, in_2}));
endmodule

module FullAdder (
  input  in_1,
  input  in_2,
  input  in_3,
  output out_4,
  output out_5
);

  wire not_1_out;

  Multiplexer #(.select(2), .enable("false")) multiplexer_1 (
    .in0(1'b0), .in1(in_1), .in2(in_1), .in3(1'b1), .out(out_4), .sel({in_2, in_3}));
  Multiplexer #(.select(2), .enable("false")) multiplexer_2 (
    .in0(in_1), .in1(not_1_out), .in2(not_1_out), .in3(in_1), .out(out_5), .sel({in_3, in_2}));
  not not_1 (not_1_out, in_1);
endmodule
